// Logisim project arm.circ as structural Verilog: 1 circuit, main circuit main
module main (
  input  in_1,
  input  [7:0] in_2,
  input  [7:0] in_3,
  output [7:0] out_4,
  output out_5,
  output [7:0] out_6,
  output CARRY,
  output OVERFLOW,
  output [2:0] out_9,
  output out_10
);

  wire adder_2_cout;
  wire [6:0] adder_2_out;

  Adder adder_1 (.a(in_2), .b(in_3), .out(out_6), .cin(in_1), .cout(CARRY));
  Subtractor subtractor_1 (.a(in_2), .b(in_3), .out(out_4), .bout(out_5));  // open: bin
  BitFinder #(.\type ("high1")) bitfinder_1 (.in(in_3), .index(out_9), .found(out_10));
  Adder #(.width(7)) adder_2 (.a(in_2[6:0]), .b(in_3[6:0]), .out(adder_2_out), .cout(adder_2_cout));  // open: cin
  xor xor_1 (OVERFLOW, CARRY, adder_2_cout);
endmodule
