// Logisim project cpu.circ as structural Verilog: 9 circuits, main circuit computer
// ALU
module alu (
  input  [15:0] A,
  input  [15:0] B,
  input  [3:0] OP,
  output EQ,
  output LT,
  output [15:0] RESULT,
  output [15:0] HI
);

  wire [15:0] adder_1_out, and_1_out, divider_1_out, divider_1_rem, multiplier_1_cout, multiplier_1_out,
       nor_1_out, or_1_out, shifter_1_out, shifter_2_out, shifter_3_out, subtractor_1_out, xor_1_out;

  Comparator #(.width(16)) comparator_1 (.a(A), .b(B), .eq(EQ), .lt(LT));  // open: gt
  Adder #(.width(16)) adder_1 (.a(A), .b(B), .out(adder_1_out));  // open: cin, cout
  Subtractor #(.width(16)) subtractor_1 (.a(A), .b(B), .out(subtractor_1_out));  // open: bin, bout
  Shifter #(.width(16)) shifter_1 (.in(A), .\dist (B[3:0]), .out(shifter_1_out));
  Shifter #(.width(16), .shift("lr")) shifter_2 (.in(A), .\dist (B[3:0]), .out(shifter_2_out));
  Shifter #(.width(16), .shift("ar")) shifter_3 (.in(A), .\dist (B[3:0]), .out(shifter_3_out));
  assign and_1_out = A & B;  // AND_Gate and_1, 16 bits wide
  assign or_1_out = A | B;  // OR_Gate or_1, 16 bits wide
  assign nor_1_out = ~(A | B);  // NOR_Gate nor_1, 16 bits wide
  assign xor_1_out = A ^ B;  // XOR_Gate xor_1, 16 bits wide
  Multiplier #(.width(16)) multiplier_1 (.a(A), .b(B), .out(multiplier_1_out), .cout(multiplier_1_cout));  // open: cin
  Divider #(.width(16)) divider_1 (.a(A), .b(B), .out(divider_1_out), .rem(divider_1_rem));  // open: upper
  Multiplexer #(.select(4), .width(16), .enable("false")) multiplexer_1 (
    .in0(adder_1_out), .in1(subtractor_1_out), .in2(shifter_1_out), .in3(shifter_2_out), .in4(shifter_3_out),
    .in5(and_1_out), .in6(or_1_out), .in7(nor_1_out), .in8(xor_1_out), .in9(multiplier_1_out),
    .in10(divider_1_out), .out(RESULT), .sel(OP));  // open: in11, in12, in13, in14, in15
  Multiplexer #(.select(4), .width(16), .enable("false")) multiplexer_2 (
    .in9(multiplier_1_cout), .in10(divider_1_rem), .out(HI), .sel(OP));  // open: in0, in1, in2, in3, in4, in5, in6, in7, in8, in11, in12, in13, in14, in15
  Pull_Resistor pull_resistor_1 (.node(RESULT));
  Pull_Resistor pull_resistor_2 (.node(HI));
endmodule

// CPU
module cpu (
  input  CLOCK_IN,
  input  RESET,
  input  [15:0] DATA_IN,
  output MEM_WRT,
  output [15:0] DATA_OUT,
  output [15:0] ADDRESS,
  output HALT
);

  wire alu_1_eq, alu_1_lt, controlled_buffer_1_out, d_ff_1_q, FETCH_q, mc_control_1_alu_b_src,
       mc_control_1_fetch_2, mc_control_1_hi_wrt, mc_control_1_ir_wrt, mc_control_1_lo_wrt,
       mc_control_1_op_wrt, mc_control_1_reg_src2_src, mc_control_1_reg_write, mc_control_1_result_wrt,
       mc_control_1_t_reset, multiplexer_2_out, not_1_out, not_2_out, not_3_out, or_1_out;
  wire [1:0] mc_control_1_mar_src, mc_control_1_pc_src, mc_control_1_pc_wrt;
  wire [2:0] mc_control_1_reg_src;
  wire [3:0] IR_q, IR_q_2, mc_control_1_alu_op, multiplexer_6_out, T_q;
  wire [7:0] IR_q_3;
  wire [11:0] OP_q;
  wire [15:0] adder_1_out, adder_2_out, adder_3_out, alu_1_hi, alu_1_result, bit_extender_1_out, HI_q, LO_q,
       multiplexer_1_out, multiplexer_4_out, multiplexer_5_out, PC_q, reg_1_src1_out, RESULT_q, shifter_1_out;
  wire [15:12] OP_q_2;

  Shifter #(.width(16)) shifter_1 (.in({OP_q_2, OP_q}), .\dist (4'b0001), .out(shifter_1_out));
  not not_1 (not_1_out, alu_1_eq);
  assign controlled_buffer_1_out = not_2_out ? CLOCK_IN : 1'bz;  // Controlled_Buffer controlled_buffer_1
  not not_2 (not_2_out, HALT);
  Adder #(.width(16)) adder_1 (.a(PC_q), .b(shifter_1_out), .out(adder_1_out));  // open: cin, cout
  Adder #(.width(16)) adder_2 (.a(PC_q), .b(16'h2), .out(adder_2_out));  // open: cin, cout
  not not_3 (not_3_out, controlled_buffer_1_out);
  // Probe on adder_1_out
  Multiplexer #(.select(2), .width(16), .enable("false")) multiplexer_1 (
    .in0(adder_2_out), .in1(adder_1_out), .in2({OP_q_2, OP_q}), .in3(DATA_OUT), .out(multiplexer_1_out),
    .sel(mc_control_1_pc_src));
  Counter #(.width(4), .max('hf)) T (.Q(T_q), .clk(not_3_out), .clr(or_1_out));  // open: load, D, count, carry
  Register #(.width(16)) PC (
    .D(multiplexer_1_out), .en(multiplexer_2_out), .Q(PC_q), .clk(controlled_buffer_1_out), .clr(RESET));
  Multiplexer #(.select(2), .enable("false")) multiplexer_2 (
    .in0(1'b0), .in1(1'b1), .in2(alu_1_eq), .in3(not_1_out), .out(multiplexer_2_out),
    .sel(mc_control_1_pc_wrt));
  D_Flip_Flop FETCH (.clk(not_3_out), .D(mc_control_1_fetch_2), .Q(FETCH_q), .preset(RESET));  // open: Qn, en, reset
  or or_1 (or_1_out, d_ff_1_q, RESET);
  D_Flip_Flop d_ff_1 (.clk(not_3_out), .D(mc_control_1_t_reset), .Q(d_ff_1_q));  // open: Qn, preset, en, reset
  Adder #(.width(16)) adder_3 (.a(PC_q), .b(16'h1), .out(adder_3_out));  // open: cin, cout
  mc_control mc_control_1 (
    .INSTRUCTION(IR_q_3[4:0]), .FETCH(FETCH_q), .T(T_q), .HALT(HALT), .T_RESET(mc_control_1_t_reset),
    .FETCH_2(mc_control_1_fetch_2), .PC_SRC(mc_control_1_pc_src), .PC_WRT(mc_control_1_pc_wrt),
    .MAR_SRC(mc_control_1_mar_src), .MEM_WRT(MEM_WRT), .IR_WRT(mc_control_1_ir_wrt),
    .OP_WRT(mc_control_1_op_wrt), .REG_SRC(mc_control_1_reg_src), .REG_WRITE(mc_control_1_reg_write),
    .ALU_B_SRC(mc_control_1_alu_b_src), .REG_SRC2_SRC(mc_control_1_reg_src2_src),
    .ALU_OP(mc_control_1_alu_op), .RESULT_WRT(mc_control_1_result_wrt), .LO_WRT(mc_control_1_lo_wrt),
    .HI_WRT(mc_control_1_hi_wrt));
  Register #(.width(16)) IR (
    .D(DATA_IN), .en(mc_control_1_ir_wrt), .Q({IR_q_3, IR_q_2, IR_q}), .clk(controlled_buffer_1_out));  // open: clr
  Multiplexer #(.select(2), .width(16), .enable("false")) multiplexer_3 (
    .in0(PC_q), .in1(adder_3_out), .in2(RESULT_q), .out(ADDRESS), .sel(mc_control_1_mar_src));  // open: in3
  // Probe on DATA_IN
  Multiplexer #(.select(3), .width(16), .enable("false")) multiplexer_4 (
    .in0(RESULT_q), .in1(bit_extender_1_out), .in2(PC_q), .in3(HI_q), .in4(LO_q), .in5(DATA_IN),
    .out(multiplexer_4_out), .sel(mc_control_1_reg_src));  // open: in6, in7
  Register #(.width(16)) OP (
    .D(DATA_IN), .en(mc_control_1_op_wrt), .Q({OP_q_2, OP_q}), .clk(controlled_buffer_1_out));  // open: clr
  // Probe on DATA_OUT
  \reg  reg_1 (
    .SRC1_REG(IR_q), .SRC2_REG(multiplexer_6_out), .CLOCK(controlled_buffer_1_out),
    .WRITE(mc_control_1_reg_write), .DATA_IN(multiplexer_4_out), .DST_REG(IR_q_2), .SRC1_OUT(reg_1_src1_out),
    .SRC2_OUT(DATA_OUT));
  Multiplexer #(.width(16), .enable("false")) multiplexer_5 (
    .in0(DATA_OUT), .in1({OP_q_2, OP_q}), .out(multiplexer_5_out), .sel(mc_control_1_alu_b_src));
  Multiplexer #(.width(4), .enable("false")) multiplexer_6 (
    .in0(OP_q_2), .in1(IR_q_2), .out(multiplexer_6_out), .sel(mc_control_1_reg_src2_src));
  alu alu_1 (
    .A(reg_1_src1_out), .B(multiplexer_5_out), .OP(mc_control_1_alu_op), .EQ(alu_1_eq), .LT(alu_1_lt),
    .RESULT(alu_1_result), .HI(alu_1_hi));
  Register #(.width(16)) LO (
    .D(alu_1_result), .en(mc_control_1_lo_wrt), .Q(LO_q), .clk(controlled_buffer_1_out));  // open: clr
  assign bit_extender_1_out = {{15{1'b0}}, alu_1_lt};  // Bit_Extender bit_extender_1
  Register #(.width(16)) HI (
    .D(alu_1_hi), .en(mc_control_1_hi_wrt), .Q(HI_q), .clk(controlled_buffer_1_out));  // open: clr
  Register #(.width(16)) RESULT (
    .D(alu_1_result), .en(mc_control_1_result_wrt), .Q(RESULT_q), .clk(controlled_buffer_1_out));  // open: clr
endmodule

// REG
module \reg  (
  input  [3:0] SRC1_REG,
  input  [3:0] SRC2_REG,
  input  CLOCK,
  input  WRITE,
  input  [15:0] DATA_IN,
  input  [3:0] DST_REG,
  output [15:0] SRC1_OUT,
  output [15:0] SRC2_OUT
);

  wire and_1_out, and_2_out, and_3_out, and_4_out, and_5_out, and_6_out, and_7_out, and_8_out, and_9_out,
       and_10_out, and_11_out, and_12_out, and_13_out, and_14_out, and_15_out, decoder_1_out1,
       decoder_1_out2, decoder_1_out3, decoder_1_out4, decoder_1_out5, decoder_1_out6, decoder_1_out7,
       decoder_1_out8, decoder_1_out9, decoder_1_out10, decoder_1_out11, decoder_1_out12, decoder_1_out13,
       decoder_1_out14, decoder_1_out15, decoder_2_out0, decoder_2_out1, decoder_2_out2, decoder_2_out3,
       decoder_2_out4, decoder_2_out5, decoder_2_out6, decoder_2_out7, decoder_2_out8, decoder_2_out9,
       decoder_2_out10, decoder_2_out11, decoder_2_out12, decoder_2_out13, decoder_2_out14, decoder_2_out15,
       decoder_3_out0, decoder_3_out1, decoder_3_out2, decoder_3_out3, decoder_3_out4, decoder_3_out5,
       decoder_3_out6, decoder_3_out7, decoder_3_out8, decoder_3_out9, decoder_3_out10, decoder_3_out11,
       decoder_3_out12, decoder_3_out13, decoder_3_out14, decoder_3_out15;
  wire [15:0] R1_q, R2_q, R3_q, R4_q, R5_q, R6_q, R7_q, R8_q, R9_q, R10_q, R11_q, R12_q, R13_q, R14_q, R15_q;

  Decoder #(.select(4), .enable("false")) decoder_1 (
    .out1(decoder_1_out1), .out2(decoder_1_out2), .out3(decoder_1_out3), .out4(decoder_1_out4),
    .out5(decoder_1_out5), .out6(decoder_1_out6), .out7(decoder_1_out7), .out8(decoder_1_out8),
    .out9(decoder_1_out9), .out10(decoder_1_out10), .out11(decoder_1_out11), .out12(decoder_1_out12),
    .out13(decoder_1_out13), .out14(decoder_1_out14), .out15(decoder_1_out15), .sel(DST_REG));  // open: out0
  and and_1 (and_1_out, decoder_1_out1, WRITE);
  and and_2 (and_2_out, decoder_1_out2, WRITE);
  and and_3 (and_3_out, decoder_1_out3, WRITE);
  and and_4 (and_4_out, decoder_1_out4, WRITE);
  and and_5 (and_5_out, decoder_1_out5, WRITE);
  and and_6 (and_6_out, decoder_1_out6, WRITE);
  and and_7 (and_7_out, decoder_1_out7, WRITE);
  and and_8 (and_8_out, decoder_1_out8, WRITE);
  and and_9 (and_9_out, decoder_1_out9, WRITE);
  and and_10 (and_10_out, decoder_1_out10, WRITE);
  and and_11 (and_11_out, decoder_1_out11, WRITE);
  and and_12 (and_12_out, decoder_1_out12, WRITE);
  and and_13 (and_13_out, decoder_1_out13, WRITE);
  and and_14 (and_14_out, decoder_1_out14, WRITE);
  and and_15 (and_15_out, decoder_1_out15, WRITE);
  Register #(.width(16)) R1 (.D(DATA_IN), .en(and_1_out), .Q(R1_q), .clk(CLOCK));  // open: clr
  Register #(.width(16)) R2 (.D(DATA_IN), .en(and_2_out), .Q(R2_q), .clk(CLOCK));  // open: clr
  Register #(.width(16)) R3 (.D(DATA_IN), .en(and_3_out), .Q(R3_q), .clk(CLOCK));  // open: clr
  Register #(.width(16)) R4 (.D(DATA_IN), .en(and_4_out), .Q(R4_q), .clk(CLOCK));  // open: clr
  Register #(.width(16)) R5 (.D(DATA_IN), .en(and_5_out), .Q(R5_q), .clk(CLOCK));  // open: clr
  Register #(.width(16)) R6 (.D(DATA_IN), .en(and_6_out), .Q(R6_q), .clk(CLOCK));  // open: clr
  Register #(.width(16)) R7 (.D(DATA_IN), .en(and_7_out), .Q(R7_q), .clk(CLOCK));  // open: clr
  Register #(.width(16)) R8 (.D(DATA_IN), .en(and_8_out), .Q(R8_q), .clk(CLOCK));  // open: clr
  Register #(.width(16)) R9 (.D(DATA_IN), .en(and_9_out), .Q(R9_q), .clk(CLOCK));  // open: clr
  Register #(.width(16)) R10 (.D(DATA_IN), .en(and_10_out), .Q(R10_q), .clk(CLOCK));  // open: clr
  Register #(.width(16)) R11 (.D(DATA_IN), .en(and_11_out), .Q(R11_q), .clk(CLOCK));  // open: clr
  Register #(.width(16)) R12 (.D(DATA_IN), .en(and_12_out), .Q(R12_q), .clk(CLOCK));  // open: clr
  Register #(.width(16)) R13 (.D(DATA_IN), .en(and_13_out), .Q(R13_q), .clk(CLOCK));  // open: clr
  Register #(.width(16)) R14 (.D(DATA_IN), .en(and_14_out), .Q(R14_q), .clk(CLOCK));  // open: clr
  Register #(.width(16)) R15 (.D(DATA_IN), .en(and_15_out), .Q(R15_q), .clk(CLOCK));  // open: clr
  Decoder #(.select(4), .enable("false")) decoder_2 (
    .out0(decoder_2_out0), .out1(decoder_2_out1), .out2(decoder_2_out2), .out3(decoder_2_out3),
    .out4(decoder_2_out4), .out5(decoder_2_out5), .out6(decoder_2_out6), .out7(decoder_2_out7),
    .out8(decoder_2_out8), .out9(decoder_2_out9), .out10(decoder_2_out10), .out11(decoder_2_out11),
    .out12(decoder_2_out12), .out13(decoder_2_out13), .out14(decoder_2_out14), .out15(decoder_2_out15),
    .sel(SRC1_REG));
  assign SRC1_OUT = decoder_2_out0 ? {16{1'b0}} : 16'bz;  // Controlled_Buffer controlled_buffer_1
  assign SRC1_OUT = decoder_2_out1 ? R1_q : 16'bz;  // Controlled_Buffer controlled_buffer_2
  assign SRC1_OUT = decoder_2_out2 ? R2_q : 16'bz;  // Controlled_Buffer controlled_buffer_3
  assign SRC1_OUT = decoder_2_out3 ? R3_q : 16'bz;  // Controlled_Buffer controlled_buffer_4
  assign SRC1_OUT = decoder_2_out4 ? R4_q : 16'bz;  // Controlled_Buffer controlled_buffer_5
  assign SRC1_OUT = decoder_2_out5 ? R5_q : 16'bz;  // Controlled_Buffer controlled_buffer_6
  assign SRC1_OUT = decoder_2_out6 ? R6_q : 16'bz;  // Controlled_Buffer controlled_buffer_7
  assign SRC1_OUT = decoder_2_out7 ? R7_q : 16'bz;  // Controlled_Buffer controlled_buffer_8
  assign SRC1_OUT = decoder_2_out8 ? R8_q : 16'bz;  // Controlled_Buffer controlled_buffer_9
  assign SRC1_OUT = decoder_2_out9 ? R9_q : 16'bz;  // Controlled_Buffer controlled_buffer_10
  assign SRC1_OUT = decoder_2_out10 ? R10_q : 16'bz;  // Controlled_Buffer controlled_buffer_11
  assign SRC1_OUT = decoder_2_out11 ? R11_q : 16'bz;  // Controlled_Buffer controlled_buffer_12
  assign SRC1_OUT = decoder_2_out12 ? R12_q : 16'bz;  // Controlled_Buffer controlled_buffer_13
  assign SRC1_OUT = decoder_2_out13 ? R13_q : 16'bz;  // Controlled_Buffer controlled_buffer_14
  assign SRC1_OUT = decoder_2_out14 ? R14_q : 16'bz;  // Controlled_Buffer controlled_buffer_15
  assign SRC1_OUT = decoder_2_out15 ? R15_q : 16'bz;  // Controlled_Buffer controlled_buffer_16
  Decoder #(.select(4), .enable("false")) decoder_3 (
    .out0(decoder_3_out0), .out1(decoder_3_out1), .out2(decoder_3_out2), .out3(decoder_3_out3),
    .out4(decoder_3_out4), .out5(decoder_3_out5), .out6(decoder_3_out6), .out7(decoder_3_out7),
    .out8(decoder_3_out8), .out9(decoder_3_out9), .out10(decoder_3_out10), .out11(decoder_3_out11),
    .out12(decoder_3_out12), .out13(decoder_3_out13), .out14(decoder_3_out14), .out15(decoder_3_out15),
    .sel(SRC2_REG));
  assign SRC2_OUT = decoder_3_out0 ? {16{1'b0}} : 16'bz;  // Controlled_Buffer controlled_buffer_17
  assign SRC2_OUT = decoder_3_out1 ? R1_q : 16'bz;  // Controlled_Buffer controlled_buffer_18
  assign SRC2_OUT = decoder_3_out2 ? R2_q : 16'bz;  // Controlled_Buffer controlled_buffer_19
  assign SRC2_OUT = decoder_3_out3 ? R3_q : 16'bz;  // Controlled_Buffer controlled_buffer_20
  assign SRC2_OUT = decoder_3_out4 ? R4_q : 16'bz;  // Controlled_Buffer controlled_buffer_21
  assign SRC2_OUT = decoder_3_out5 ? R5_q : 16'bz;  // Controlled_Buffer controlled_buffer_22
  assign SRC2_OUT = decoder_3_out6 ? R6_q : 16'bz;  // Controlled_Buffer controlled_buffer_23
  assign SRC2_OUT = decoder_3_out7 ? R7_q : 16'bz;  // Controlled_Buffer controlled_buffer_24
  assign SRC2_OUT = decoder_3_out8 ? R8_q : 16'bz;  // Controlled_Buffer controlled_buffer_25
  assign SRC2_OUT = decoder_3_out9 ? R9_q : 16'bz;  // Controlled_Buffer controlled_buffer_26
  assign SRC2_OUT = decoder_3_out10 ? R10_q : 16'bz;  // Controlled_Buffer controlled_buffer_27
  assign SRC2_OUT = decoder_3_out11 ? R11_q : 16'bz;  // Controlled_Buffer controlled_buffer_28
  assign SRC2_OUT = decoder_3_out12 ? R12_q : 16'bz;  // Controlled_Buffer controlled_buffer_29
  assign SRC2_OUT = decoder_3_out13 ? R13_q : 16'bz;  // Controlled_Buffer controlled_buffer_30
  assign SRC2_OUT = decoder_3_out14 ? R14_q : 16'bz;  // Controlled_Buffer controlled_buffer_31
  assign SRC2_OUT = decoder_3_out15 ? R15_q : 16'bz;  // Controlled_Buffer controlled_buffer_32

  // Notes on the sheet:
  //   R0 ZERO
endmodule

// CONTROL
module mc_control (
  input  [4:0] INSTRUCTION,
  input  FETCH,
  input  [3:0] T,
  output HALT,
  output T_RESET,
  output FETCH_2,
  output [1:0] PC_SRC,
  output [1:0] PC_WRT,
  output [1:0] MAR_SRC,
  output MEM_WRT,
  output IR_WRT,
  output OP_WRT,
  output [2:0] REG_SRC,
  output REG_WRITE,
  output ALU_B_SRC,
  output REG_SRC2_SRC,
  output [3:0] ALU_OP,
  output RESULT_WRT,
  output LO_WRT,
  output HI_WRT
);

  wire [4:0] multiplexer_1_out;

  Multiplexer #(.width(5), .enable("false")) multiplexer_1 (
    .in0(INSTRUCTION), .in1({5{1'b0}}), .out(multiplexer_1_out), .sel(FETCH));
  // Probe on {2'b00, FETCH, multiplexer_1_out, T}
  ROM #(.addrWidth(12), .dataWidth(25)) rom_1 (
    .addr({2'b00, FETCH, multiplexer_1_out, T}),
    .data({HALT, T_RESET, FETCH_2, PC_SRC, PC_WRT, MAR_SRC, MEM_WRT, IR_WRT, OP_WRT, REG_SRC, REG_WRITE, ALU_B_SRC, REG_SRC2_SRC, ALU_OP, RESULT_WRT, LO_WRT, HI_WRT}));  // open: sel
  // Probe on {HALT, T_RESET, FETCH_2, PC_SRC, PC_WRT, MAR_SRC, MEM_WRT, IR_WRT, OP_WRT, REG_SRC, REG_WRITE, ALU_B_SRC, REG_SRC2_SRC, ALU_OP, RESULT_WRT, LO_WRT, HI_WRT}

  // Notes on the sheet:
  //   contents of rom_1 (hex, n*v repeats v):
  //   1000000 1000000 40004 c00200 14*1000000 40104 c00200 14*1000000 4000c c00200 14*1000000 c4004b
  //   15*1000000 c40053 15*1000000 40114 c00200 14*1000000 4011c c00200 14*1000000 40124 c00200 14*1000000
  //   40014 c00200 14*1000000 4001c c00200 14*1000000 40024 c00200 14*1000000 40000 d80080 14*1000000
  //   40000 dc0080 14*1000000 c40600 15*1000000 c40700 15*1000000 4002c c00200 14*1000000 4012c c00200
  //   14*1000000 40034 c00200 14*1000000 40134 c00200 14*1000000 40044 c00200 14*1000000 4003c c00200
  //   14*1000000 40000 e40000 14*1000000 40000 f40000 14*1000000 40000 a00 e40000 13*1000000 40000 a00
  //   f40000 13*1000000 40104 c21600 14*1000000 40104 c28080 14*1000000 c40e00 15*1000000 c41200
  //   15*1000000 c40000 45*1000000 404000 12000 3582*1000000
endmodule

module computer (
);

  wire CLK, comparator_1_eq, comparator_1_gt, counter_1_data_ready, cpu_1_mem_wrt, HLT, keyboard_1_avail,
       keyboard_io_1_char_read, keyboard_io_1_clear_buffer, keyboard_io_1_data_ready, nor_1_out, not_1_out,
       or_1_out, or_2_out, random_1_data_ready, RST, screen_io_1_screen_clear, screen_io_1_screen_out;
  wire [6:0] keyboard_1_data;
  wire [15:0] controlled_buffer_1_out, counter_1_data_out, cpu_1_address, cpu_1_data_out,
       keyboard_io_1_data_out_out, ram_1_data, random_1_data_out;

  Button RESET (.out(RST));
  Clock CLOCK (.out(CLK));
  LED HALT (.in(HLT));
  screen_io screen_io_1 (
    .ADDRESS_IN(cpu_1_address), .SCREEN_CLEAR(screen_io_1_screen_clear), .SCREEN_OUT(screen_io_1_screen_out));
  // Probe on cpu_1_data_out
  or or_1 (or_1_out, screen_io_1_screen_clear, RST);
  TTY #(.rows(16), .cols(64)) tty_1 (
    .data(cpu_1_data_out[6:0]), .clk(CLK), .we(screen_io_1_screen_out), .clr(or_1_out));
  Keyboard #(.buflen(255)) keyboard_1 (
    .clk(CLK), .re(keyboard_io_1_char_read), .clr(or_2_out), .avail(keyboard_1_avail), .data(keyboard_1_data));
  or or_2 (or_2_out, RST, keyboard_io_1_clear_buffer);
  keyboard_io keyboard_io_1 (
    .DATA_READY(keyboard_io_1_data_ready), .DATA_OUT_OUT(keyboard_io_1_data_out_out),
    .CHAR_IN(keyboard_1_data), .CHAR_READY_IN(keyboard_1_avail), .ADDRESS_IN(cpu_1_address),
    .CHAR_READ(keyboard_io_1_char_read), .CLEAR_BUFFER(keyboard_io_1_clear_buffer));
  cpu cpu_1 (
    .CLOCK_IN(CLK), .DATA_IN(controlled_buffer_1_out), .MEM_WRT(cpu_1_mem_wrt), .DATA_OUT(cpu_1_data_out),
    .ADDRESS(cpu_1_address), .RESET(RST), .HALT(HLT));
  // Probe on cpu_1_address
  not not_1 (not_1_out, cpu_1_mem_wrt);
  random random_1 (
    .ADDRESS_IN(cpu_1_address), .CLOCK(CLK), .DATA_READY(random_1_data_ready), .DATA_OUT(random_1_data_out));
  counter counter_1 (
    .CLOCK(CLK), .ADDRESS(cpu_1_address), .RESET(RST), .DATA_OUT(counter_1_data_out),
    .DATA_READY(counter_1_data_ready));
  Comparator #(.width(16), .mode("unsigned")) comparator_1 (
    .a(cpu_1_address), .b(16'hf000), .gt(comparator_1_gt), .eq(comparator_1_eq));  // open: lt
  RAM #(.addrWidth(16), .dataWidth(16), .bus("separate")) ram_1 (
    .addr(cpu_1_address), .din(cpu_1_data_out), .data(ram_1_data), .str(cpu_1_mem_wrt), .clk(CLK),
    .ld(not_1_out));  // open: sel, clr
  // Probe on controlled_buffer_1_out
  assign controlled_buffer_1_out = random_1_data_ready ? random_1_data_out : 16'bz;  // Controlled_Buffer controlled_buffer_1
  assign controlled_buffer_1_out = counter_1_data_ready ? counter_1_data_out : 16'bz;  // Controlled_Buffer controlled_buffer_2
  assign controlled_buffer_1_out = keyboard_io_1_data_ready ? keyboard_io_1_data_out_out : 16'bz;  // Controlled_Buffer controlled_buffer_3
  nor nor_1 (nor_1_out, comparator_1_gt, comparator_1_eq);
  assign controlled_buffer_1_out = nor_1_out ? ram_1_data : 16'bz;  // Controlled_Buffer controlled_buffer_4
  Pull_Resistor pull_resistor_1 (.node(controlled_buffer_1_out));

  // Notes on the sheet:
  //   ADDRESS BUS
  //   DATA OUTPUT BUS
  //   Screen
  //   Keyboard
  //   DATA INPUT BUS
  //   IO ADDRESS
  //   RAM
endmodule

// COUNT
module counter (
  input  CLOCK,
  input  [15:0] ADDRESS,
  input  RESET,
  output [15:0] DATA_OUT,
  output DATA_READY
);

  wire comparator_1_eq, comparator_2_eq, COUNT_LO_carry, d_ff_1_q;
  wire [15:0] COUNT_HI_q, COUNT_LO_q;

  Counter #(.width(16), .max('hffff)) COUNT_LO (
    .Q(COUNT_LO_q), .carry(COUNT_LO_carry), .clk(CLOCK), .clr(RESET));  // open: load, D, count
  Counter #(.width(16), .max('hffff)) COUNT_HI (
    .Q(COUNT_HI_q), .clk(d_ff_1_q), .clr(RESET));  // open: load, D, count, carry
  D_Flip_Flop d_ff_1 (.clk(CLOCK), .D(COUNT_LO_carry), .Q(d_ff_1_q));  // open: Qn, preset, en, reset
  assign DATA_OUT = comparator_2_eq ? COUNT_LO_q : 16'bz;  // Controlled_Buffer LO
  assign DATA_OUT = comparator_1_eq ? COUNT_HI_q : 16'bz;  // Controlled_Buffer HI
  Comparator #(.width(16), .mode("unsigned")) comparator_1 (
    .a(ADDRESS), .b(16'hf001), .eq(comparator_1_eq));  // open: gt, lt
  Comparator #(.width(16), .mode("unsigned")) comparator_2 (
    .a(ADDRESS), .b(16'hf000), .eq(comparator_2_eq));  // open: gt, lt
  or or_1 (DATA_READY, comparator_1_eq, comparator_2_eq);
endmodule

// RAND
module random (
  input  [15:0] ADDRESS_IN,
  input  CLOCK,
  output DATA_READY,
  output [15:0] DATA_OUT
);

  Comparator #(.width(16), .mode("unsigned")) comparator_1 (
    .a(ADDRESS_IN), .b(16'hf002), .eq(DATA_READY));  // open: gt, lt
  Random #(.width(16)) random_1 (.clk(CLOCK), .out(DATA_OUT));  // open: next, clr
endmodule

// SCRN IO
module screen_io (
  input  [15:0] ADDRESS_IN,
  output SCREEN_OUT,
  output SCREEN_CLEAR
);

  Comparator #(.width(16), .mode("unsigned")) comparator_1 (
    .a(16'hfffe), .b(ADDRESS_IN), .eq(SCREEN_OUT));  // open: gt, lt
  Comparator #(.width(16), .mode("unsigned")) comparator_2 (
    .a({16{1'b1}}), .b(ADDRESS_IN), .eq(SCREEN_CLEAR));  // open: gt, lt
endmodule

// KEY IO
module keyboard_io (
  input  [6:0] CHAR_IN,
  input  CHAR_READY_IN,
  input  [15:0] ADDRESS_IN,
  output DATA_READY,
  output [15:0] DATA_OUT_OUT,
  output CHAR_READ,
  output CLEAR_BUFFER
);

  wire comparator_3_eq;
  wire [15:0] bit_extender_1_out, bit_extender_2_out;

  or or_1 (DATA_READY, comparator_3_eq, CHAR_READ);
  assign DATA_OUT_OUT = comparator_3_eq ? bit_extender_2_out : 16'bz;  // Controlled_Buffer controlled_buffer_1
  assign DATA_OUT_OUT = CHAR_READ ? bit_extender_1_out : 16'bz;  // Controlled_Buffer controlled_buffer_2
  Comparator #(.width(16), .mode("unsigned")) comparator_1 (
    .a(ADDRESS_IN), .b(16'hfffd), .eq(CHAR_READ));  // open: gt, lt
  Comparator #(.width(16), .mode("unsigned")) comparator_2 (
    .a(ADDRESS_IN), .b(16'hfffb), .eq(CLEAR_BUFFER));  // open: gt, lt
  Comparator #(.width(16), .mode("unsigned")) comparator_3 (
    .a(ADDRESS_IN), .b(16'hfffc), .eq(comparator_3_eq));  // open: gt, lt
  assign bit_extender_1_out = {{9{1'b0}}, CHAR_IN};  // Bit_Extender bit_extender_1
  assign bit_extender_2_out = {{15{1'b0}}, CHAR_READY_IN};  // Bit_Extender bit_extender_2
endmodule
